# Fritzing sketch meteo (saved by Fritzing 0.9.2b)
breadboards: 1

parts:
  R1 = Resistor [tolerance=±5% resistance=1k package=THT]
  R2 = Resistor [tolerance=±5% resistance=1k package=THT]
  R3 = Photocell (LDR) [package=THT]
  RHT1 = Humidity and Temperature Sensor RHT03
  Part1 = Arduino Uno (Rev3)
  Part2 = FC-28 Soil Hygrometer Module
  Part3 = FC-28 Soil Hygrometer Module - Probe

nets:
  VCC: R1.Pin_0, R3.pin_1, RHT1.Vcc, Part1.D2, Part1.5V, Part2.VCC
  N1: R1.Pin_1, RHT1.Data-signal
  GND: R2.Pin_0, RHT1.GND_2, Part1.GND, Part2.GND
  N2: R2.Pin_1, R3.pin_0, Part1.A2
  N3: Part1.A4/SDA, Part2.AO
  N4: Part2.POS, Part3.POS
  N5: Part2.NEG, Part3.NEG

custom parts:
  FC-28 Soil Hygrometer Module: The FC-28 is a soil hygrometer module that uses the Texas Instruments LM393 comparator chip to provide an analog measurement of soil humidity. The digital output is high when soil moisture is over a certain threshold, as determined by adjusting the potentiometer.
  FC-28 Soil Hygrometer Module - Probe: The FC-28 is a soil hygrometer module that uses the Texas Instruments LM393 comparator chip to provide an analog measurement of soil humidity.
